# Fritzing sketch circuit (saved by Fritzing 0.9.3b)
breadboards: 1

parts:
  U1 = attiny85 [package=dip]
  Q1 = NPN-Transistor [package="TO92 [THT]"]
  LED1 = LED - 3mm [color="Infrared (850nm)" package="3 mm [THT]"]
  S1 = Pushbutton [package="[SMD]"]
  S2 = Pushbutton [package="[SMD]"]
  R1 = Resistor [tolerance=±5% resistance=470 package=THT]
  S4 = Pushbutton [package="[THT]"]
  LED2 = LED - 3mm [color="Yellow (585nm)" package="3 mm [THT]"]
  C2 = Electrolytic Capacitor [capacitance=10µF package="100 mil [THT, electrolytic]"]
  R2 = Resistor [tolerance=±5% resistance=150 package=THT]

nets:
  N1: U1.Pin_1, S1.Pin_3, S1.Pin_4
  N2: U1.Pin_3, R1.Pin_1
  N3: U1.Pin_4, Q1.E, S1.Pin_1, S1.Pin_2, S2.Pin_1, S2.Pin_2, S4.Pin_1, S4.Pin_2, C2.+
  N4: U1.Pin_5, S4.Pin_3, S4.Pin_4
  N5: U1.Pin_6, S2.Pin_3, S2.Pin_4
  N6: U1.Pin_7, R2.Pin_1
  N7: U1.Pin_8, LED1.anode, LED2.anode, C2.-
  N8: Q1.B, LED1.cathode
  N9: Q1.C, R1.Pin_0
  N10: LED2.cathode, R2.Pin_0
